# Fritzing sketch MasterCopy SmartSwitch_only CPU (saved by Fritzing 0.9.3b)
breadboards: 1

parts:
  Right = female pin header, 15 pins [form="♀ (female)"]
  Left = female pin header, 15 pins [form="♀ (female)"]
  U1 = Sharp PC847X [package=THT]  # not connected
  U2 = Sharp PC817 [package=THT]  # not connected
  U3 = Sharp PC817 [package=THT]  # not connected
  U4 = Sharp PC817 [package=THT]  # not connected
  U5 = Sharp PC817 [package=THT]  # not connected
  JRIGHT = female pin header, 15 pins [form="♀ (female)"]
  J1 = female pin header, 15 pins [form="♀ (female)"]

nets:
  STSLED: Right.pin1, JRIGHT.pin1
  OUT0: Right.pin2, JRIGHT.pin2
  OUT1: Right.pin3, JRIGHT.pin3
  OUT2: Right.pin4, JRIGHT.pin4
  OUT3: Right.pin5, JRIGHT.pin5
  VDD: Right.pin6, Right.pin15, Left.pin11, JRIGHT.pin6, J1.pin11
  GND: Right.pin7, Right.pin14, Left.pin2, Left.pin10, Left.pin14, JRIGHT.pin7, J1.pin2, J1.pin10, J1.pin14
  IN0: Right.pin8, JRIGHT.pin8
  IN1: Right.pin9, JRIGHT.pin9
  IN2: Right.pin10, JRIGHT.pin10
  IN3: Right.pin11, JRIGHT.pin11
  Ain: Left.pin1, J1.pin1
  N1: Left.pin3, J1.pin3
  GPIO10: Left.pin4, J1.pin4
  GPIO9: Left.pin5, J1.pin5
  MOSI: Left.pin6, J1.pin6
  CS: Left.pin7, J1.pin7
  MISO: Left.pin8, J1.pin8
  CLK: Left.pin9, J1.pin9
  N2: Left.pin12, J1.pin12
  N3: Left.pin13, J1.pin13
  VCC: Left.pin15, J1.pin15
