# Fritzing sketch MasterCopy_main_board_UNROUTED_Complete_16pin_opto (saved by Fritzing 0.9.3b)
breadboards: 1

parts:
  Right = female pin header, 15 pins [form="♀ (female)"]
  Left = female pin header, 15 pins [form="♀ (female)"]
  OUTPUT = Sharp PC847X [package=THT]
  JRIGHT = female pin header, 15 pins [form="♀ (female)"]
  JLeft = female pin header, 15 pins [form="♀ (female)"]
  ROUT00 = Resistor [tolerance=±5% resistance=220 package=THT]
  ROUT10 = Resistor [tolerance=±5% resistance=220 package=THT]
  ROUT20 = Resistor [tolerance=±5% resistance=220 package=THT]
  ROUT30 = Resistor [tolerance=±5% resistance=220 package=THT]
  Q1 = NPN-Transistor [package="TO92 [THT]"]
  Q2 = NPN-Transistor [package="TO92 [THT]"]
  Q3 = NPN-Transistor [package="TO92 [THT]"]
  Q4 = NPN-Transistor [package="TO92 [THT]"]
  ROUT01 = Resistor [tolerance=±5% resistance=50 package=THT]
  ROUT11 = Resistor [tolerance=±5% resistance=50 package=THT]
  ROUT21 = Resistor [tolerance=±5% resistance=50 package=THT]
  ROUT31 = Resistor [tolerance=±5% resistance=50 package=THT]
  J1 = female pin header, 5 pins [form="♀ (female)"]
  U1 = Sharp PC847X [package=THT]
  RO01 = Resistor [tolerance=±5% resistance=220 package=THT]
  RO11 = Resistor [tolerance=±5% resistance=220 package=THT]
  R021 = Resistor [tolerance=±5% resistance=220 package=THT]
  RO31 = Resistor [tolerance=±5% resistance=220 package=THT]
  RO00 = Resistor [tolerance=±5% resistance=220 package=THT]
  RO10 = Resistor [tolerance=±5% resistance=220 package=THT]
  RO20 = Resistor [tolerance=±5% resistance=220 package=THT]
  RO30 = Resistor [tolerance=±5% resistance=220 package=THT]
  CO0 = Ceramic Capacitor [capacitance=100nF package="100 mil [THT, multilayer]"]
  CO1 = Ceramic Capacitor [capacitance=100nF package="100 mil [THT, multilayer]"]
  CO2 = Ceramic Capacitor [capacitance=100nF package="100 mil [THT, multilayer]"]
  CO3 = Ceramic Capacitor [capacitance=100nF package="100 mil [THT, multilayer]"]
  INPUT = female pin header, 4 pins [form="♀ (female)"]

nets:
  STSLED: Right.pin1, JRIGHT.pin1
  OUT0: Right.pin2, OUTPUT.Pin_2, JRIGHT.pin2
  OUT1: Right.pin3, OUTPUT.Pin_4, JRIGHT.pin3
  OUT2: Right.pin4, OUTPUT.Pin_6, JRIGHT.pin4
  OUT3: Right.pin5, OUTPUT.Pin_8, JRIGHT.pin5
  VDD: Right.pin6, Right.pin15, Left.pin11, JRIGHT.pin6, JRIGHT.pin15, JLeft.pin11, ROUT00.Pin_0, ROUT10.Pin_0, ROUT20.Pin_0, ROUT30.Pin_0, U1.Pin_10, U1.Pin_12, U1.Pin_14, U1.Pin_16
  GND: Right.pin7, Right.pin14, Left.pin2, Left.pin10, Left.pin14, JRIGHT.pin7, JRIGHT.pin14, JLeft.pin2, JLeft.pin10, JLeft.pin14, Q1.E, Q2.E, Q3.E, Q4.E, U1.Pin_2, U1.Pin_4, U1.Pin_6, U1.Pin_8, RO01.Pin_0, RO11.Pin_0, R021.Pin_0, RO31.Pin_0, CO0.0, CO1.0, CO2.0, CO3.0
  IN0: Right.pin8, JRIGHT.pin8, U1.Pin_15, RO01.Pin_1
  IN1: Right.pin9, JRIGHT.pin9, U1.Pin_13, RO11.Pin_1
  IN2: Right.pin10, JRIGHT.pin10, U1.Pin_11, R021.Pin_1
  IN3: Right.pin11, JRIGHT.pin11, U1.Pin_9, RO31.Pin_1
  N1: Right.pin12, JRIGHT.pin12
  N2: Right.pin13, JRIGHT.pin13
  Ain: Left.pin1, JLeft.pin1
  N3: Left.pin3, JLeft.pin3
  GPIO10: Left.pin4, JLeft.pin4
  GPIO9: Left.pin5, JLeft.pin5
  MOSI: Left.pin6, JLeft.pin6
  CS: Left.pin7, JLeft.pin7
  MISO: Left.pin8, JLeft.pin8
  CLK: Left.pin9, JLeft.pin9
  N4: Left.pin12, JLeft.pin12
  N5: Left.pin13, JLeft.pin13
  VCC: Left.pin15, OUTPUT.Pin_10, OUTPUT.Pin_12, OUTPUT.Pin_14, OUTPUT.Pin_16, JLeft.pin15, J1.pin1
  N6: OUTPUT.Pin_1, ROUT00.Pin_1
  N7: OUTPUT.Pin_3, ROUT10.Pin_1
  N8: OUTPUT.Pin_5, ROUT20.Pin_1
  N9: OUTPUT.Pin_7, ROUT30.Pin_1
  N10: OUTPUT.Pin_9, ROUT31.Pin_0
  N11: OUTPUT.Pin_11, ROUT21.Pin_0
  N12: OUTPUT.Pin_13, ROUT11.Pin_0
  N13: OUTPUT.Pin_15, ROUT01.Pin_0
  N14: Q1.B, ROUT01.Pin_1
  R0: Q1.C, J1.pin2
  N15: Q2.B, ROUT11.Pin_1
  R1: Q2.C, J1.pin3
  N16: Q3.B, ROUT21.Pin_1
  R2: Q3.C, J1.pin4
  N17: Q4.B, ROUT31.Pin_1
  R3: Q4.C, J1.pin5
  N18: U1.Pin_1, RO00.Pin_0, CO0.1
  N19: U1.Pin_3, RO10.Pin_0, CO1.1
  N20: U1.Pin_5, RO20.Pin_0, CO2.1
  N21: U1.Pin_7, RO30.Pin_0, CO3.1
  B0: RO00.Pin_1, INPUT.pin1
  B1: RO10.Pin_1, INPUT.pin2
  B2: RO20.Pin_1, INPUT.pin3
  B3: RO30.Pin_1, INPUT.pin4

notes:
  OUTPUT CKT
  MAIN BOOARD, 1.0
  OUTPUT, 1.0
