# Fritzing sketch MasterCopy_main_board_UNROUTED_Complete_4pin_opto (saved by Fritzing 0.9.3b)
breadboards: 1

parts:
  Right = female pin header, 15 pins [form="♀ (female)"]
  Left = female pin header, 15 pins [form="♀ (female)"]
  JRIGHT = female pin header, 15 pins [form="♀ (female)"]
  JLeft = female pin header, 15 pins [form="♀ (female)"]
  ROUT00 = Resistor [tolerance=±5% resistance=220 package=THT]
  ROUT10 = Resistor [tolerance=±5% resistance=220 package=THT]
  ROUT20 = Resistor [tolerance=±5% resistance=220 package=THT]
  ROUT30 = Resistor [tolerance=±5% resistance=220 package=THT]
  Q1 = NPN-Transistor [package="TO92 [THT]"]
  Q2 = NPN-Transistor [package="TO92 [THT]"]
  Q3 = NPN-Transistor [package="TO92 [THT]"]
  Q4 = NPN-Transistor [package="TO92 [THT]"]
  ROUT01 = Resistor [tolerance=±5% resistance=50 package=THT]
  ROUT11 = Resistor [tolerance=±5% resistance=50 package=THT]
  ROUT21 = Resistor [tolerance=±5% resistance=50 package=THT]
  ROUT31 = Resistor [tolerance=±5% resistance=50 package=THT]
  J1 = female pin header, 5 pins [form="♀ (female)"]
  RI01 = Resistor [tolerance=±5% resistance=220 package=THT]
  RI11 = Resistor [tolerance=±5% resistance=220 package=THT]
  RI21 = Resistor [tolerance=±5% resistance=220 package=THT]
  RI31 = Resistor [tolerance=±5% resistance=220 package=THT]
  RI00 = Resistor [tolerance=±5% resistance=220 package=THT]
  RI10 = Resistor [tolerance=±5% resistance=220 package=THT]
  RI20 = Resistor [tolerance=±5% resistance=220 package=THT]
  RI30 = Resistor [tolerance=±5% resistance=220 package=THT]
  CI0 = Ceramic Capacitor [capacitance=100nF package="100 mil [THT, multilayer]"]
  CI1 = Ceramic Capacitor [capacitance=100nF package="100 mil [THT, multilayer]"]
  CI2 = Ceramic Capacitor [capacitance=100nF package="100 mil [THT, multilayer]"]
  CI3 = Ceramic Capacitor [capacitance=100nF package="100 mil [THT, multilayer]"]
  INPUT = female pin header, 4 pins [form="♀ (female)"]
  O0 = Sharp PC817 [package=THT]
  O1 = Sharp PC817 [package=THT]
  O2 = Sharp PC817 [package=THT]
  O3 = Sharp PC817 [package=THT]
  I0 = Sharp PC817 [package=THT]
  I1 = Sharp PC817 [package=THT]
  I2 = Sharp PC817 [package=THT]
  I3 = Sharp PC817 [package=THT]

nets:
  STSLED: Right.pin1, JRIGHT.pin1
  OUT0: Right.pin2, JRIGHT.pin2, O0.Pin_2
  OUT1: Right.pin3, JRIGHT.pin3, O1.Pin_2
  OUT2: Right.pin4, JRIGHT.pin4, O2.Pin_2
  OUT3: Right.pin5, JRIGHT.pin5, O3.Pin_2
  VDD: Right.pin6, Right.pin15, Left.pin11, JRIGHT.pin6, JRIGHT.pin15, JLeft.pin11, ROUT00.Pin_0, ROUT10.Pin_0, ROUT20.Pin_0, ROUT30.Pin_0, I0.Pin_1, I1.Pin_1, I2.Pin_1, I3.Pin_1
  GND: Right.pin7, Right.pin14, Left.pin2, Left.pin10, Left.pin14, JRIGHT.pin7, JRIGHT.pin14, JLeft.pin2, JLeft.pin10, JLeft.pin14, Q1.E, Q2.E, Q3.E, Q4.E, RI01.Pin_0, RI11.Pin_0, RI21.Pin_0, RI31.Pin_0, CI0.0, CI1.0, CI2.0, CI3.0, I0.Pin_3, I1.Pin_3, I2.Pin_3, I3.Pin_3
  IN0: Right.pin8, JRIGHT.pin8, RI01.Pin_1, I0.Pin_2
  IN1: Right.pin9, JRIGHT.pin9, RI11.Pin_1, I1.Pin_2
  IN2: Right.pin10, JRIGHT.pin10, RI21.Pin_1, I2.Pin_2
  IN3: Right.pin11, JRIGHT.pin11, RI31.Pin_1, I3.Pin_2
  N1: Right.pin12, JRIGHT.pin12
  N2: Right.pin13, JRIGHT.pin13
  Ain: Left.pin1, JLeft.pin1
  N3: Left.pin3, JLeft.pin3
  GPIO10: Left.pin4, JLeft.pin4
  GPIO9: Left.pin5, JLeft.pin5
  MOSI: Left.pin6, JLeft.pin6
  CS: Left.pin7, JLeft.pin7
  MISO: Left.pin8, JLeft.pin8
  CLK: Left.pin9, JLeft.pin9
  N4: Left.pin12, JLeft.pin12
  N5: Left.pin13, JLeft.pin13
  VCC: Left.pin15, JLeft.pin15, J1.pin1, O0.Pin_4, O1.Pin_4, O2.Pin_4, O3.Pin_4
  N6: ROUT00.Pin_1, O0.Pin_1
  N7: ROUT10.Pin_1, O1.Pin_1
  N8: ROUT20.Pin_1, O2.Pin_1
  N9: ROUT30.Pin_1, O3.Pin_1
  N10: Q1.B, ROUT01.Pin_1
  R0: Q1.C, J1.pin2
  N11: Q2.B, ROUT11.Pin_1
  R1: Q2.C, J1.pin3
  N12: Q3.B, ROUT21.Pin_1
  R2: Q3.C, J1.pin4
  N13: Q4.B, ROUT31.Pin_1
  R3: Q4.C, J1.pin5
  N14: ROUT01.Pin_0, O0.Pin_3
  N15: ROUT11.Pin_0, O1.Pin_3
  N16: ROUT21.Pin_0, O2.Pin_3
  N17: ROUT31.Pin_0, O3.Pin_3
  N18: RI00.Pin_0, CI0.1, I0.Pin_4
  B0: RI00.Pin_1, INPUT.pin1
  N19: RI10.Pin_0, CI1.1, I1.Pin_4
  B1: RI10.Pin_1, INPUT.pin2
  N20: RI20.Pin_0, CI2.1, I2.Pin_4
  B2: RI20.Pin_1, INPUT.pin3
  N21: RI30.Pin_0, CI3.1, I3.Pin_4
  B3: RI30.Pin_1, INPUT.pin4

notes:
  OUTPUT CKT
  MAIN BOOARD, 1.0
  OUTPUT, 1.0
