# Fritzing sketch SmartSwitch_ROUTED_Complete_4pin_opto (saved by Fritzing 0.9.3b)
circuit board: 10cm x 7cm
breadboards: 1

parts:
  Right = female pin header, 15 pins [form="♀ (female)"]
  Left = female pin header, 15 pins [form="♀ (female)"]
  JRIGHT = female pin header, 15 pins [form="♀ (female)"]
  JLeft = female pin header, 15 pins [form="♀ (female)"]
  ROUT00 = Resistor [tolerance=±5% resistance=47 package=THT]
  ROUT10 = Resistor [tolerance=±5% resistance=220 package=THT]
  ROUT20 = Resistor [tolerance=±5% resistance=220 package=THT]
  ROUT30 = Resistor [tolerance=±5% resistance=220 package=THT]
  OT1 = NPN-Transistor [package="TO92 [THT]"]
  OT2 = NPN-Transistor [package="TO92 [THT]"]
  OT3 = NPN-Transistor [package="TO92 [THT]"]
  OT4 = NPN-Transistor [package="TO92 [THT]"]
  ROUT01 = Resistor [tolerance=±5% resistance=50 package=THT]
  ROUT11 = Resistor [tolerance=±5% resistance=50 package=THT]
  ROUT21 = Resistor [tolerance=±5% resistance=50 package=THT]
  ROUT31 = Resistor [tolerance=±5% resistance=50 package=THT]
  OUTPUT = female pin header, 5 pins [form="♀ (female)"]
  RI01 = Resistor [tolerance=±5% resistance=47 package=THT]
  RI11 = Resistor [tolerance=±5% resistance=47 package=THT]
  RI21 = Resistor [tolerance=±5% resistance=220 package=THT]
  RI31 = Resistor [tolerance=±5% resistance=47 package=THT]
  RI00 = Resistor [tolerance=±5% resistance=220 package=THT]
  RI10 = Resistor [tolerance=±5% resistance=47 package=THT]
  RI20 = Resistor [tolerance=±5% resistance=220 package=THT]
  RI30 = Resistor [tolerance=±5% resistance=220 package=THT]
  INPUT = female pin header, 4 pins [form="♀ (female)"]
  O0 = Sharp PC817 [package=THT]
  O1 = Sharp PC817 [package=THT]
  O2 = Sharp PC817 [package=THT]
  O3 = Sharp PC817 [package=THT]
  IN0 = Sharp PC817 [package=THT]
  IN1 = Sharp PC817 [package=THT]
  IN2 = Sharp PC817 [package=THT]
  IN3 = Sharp PC817 [package=THT]
  STSR = Resistor [tolerance=±5% resistance=220 package=THT]
  LED1 = LED - 3mm [color="Red (633nm)" package="3 mm [THT]"]

nets:
  STSLED: Right.pin1, JRIGHT.pin1, STSR.Pin_0
  OUT0: Right.pin2, JRIGHT.pin2, O0.Pin_2
  OUT1: Right.pin3, JRIGHT.pin3, O1.Pin_2
  OUT2: Right.pin4, JRIGHT.pin4, O2.Pin_2
  OUT3: Right.pin5, JRIGHT.pin5, O3.Pin_2
  VDDR0: Right.pin6, JRIGHT.pin6, ROUT30.Pin_0
  GNDR0: Right.pin7, JRIGHT.pin7, OT1.E, OT2.E, OT3.E, OT4.E
  IN0: Right.pin8, JRIGHT.pin8, RI00.Pin_0, IN0.Pin_3
  IN1: Right.pin9, JRIGHT.pin9, RI10.Pin_0, IN1.Pin_3
  IN2: Right.pin10, JRIGHT.pin10, RI20.Pin_0, IN2.Pin_3
  IN3: Right.pin11, JRIGHT.pin11, RI30.Pin_0, IN3.Pin_3
  N1: Right.pin12, JRIGHT.pin12
  N2: Right.pin13, JRIGHT.pin13
  GNDR1: Right.pin14, JRIGHT.pin14, RI00.Pin_1, RI10.Pin_1, IN0.Pin_2, IN1.Pin_2
  VDDR1: Right.pin15, JRIGHT.pin15, IN0.Pin_4, IN1.Pin_4
  Ain: Left.pin1, JLeft.pin1
  N3: Left.pin2, JLeft.pin2
  N4: Left.pin3, JLeft.pin3
  GPIO10: Left.pin4, JLeft.pin4
  GPIO9: Left.pin5, JLeft.pin5
  MOSI: Left.pin6, JLeft.pin6
  CS: Left.pin7, JLeft.pin7
  MISO: Left.pin8, JLeft.pin8
  CLK: Left.pin9, JLeft.pin9
  GNDL1: Left.pin10, JLeft.pin10, RI20.Pin_1, IN2.Pin_2
  VDDL: Left.pin11, JLeft.pin11, ROUT00.Pin_0, ROUT10.Pin_0, ROUT20.Pin_0, IN2.Pin_4, IN3.Pin_4, LED1.anode
  N5: Left.pin12, JLeft.pin12
  N6: Left.pin13, JLeft.pin13
  GNDL2: Left.pin14, JLeft.pin14, RI30.Pin_1, IN3.Pin_2
  VCC: Left.pin15, JLeft.pin15, OUTPUT.pin1, O0.Pin_4, O1.Pin_4, O2.Pin_4, O3.Pin_4
  N7: ROUT00.Pin_1, O0.Pin_1
  N8: ROUT10.Pin_1, O1.Pin_1
  N9: ROUT20.Pin_1, O2.Pin_1
  N10: ROUT30.Pin_1, O3.Pin_1
  N11: OT1.B, ROUT01.Pin_1
  R0: OT1.C, OUTPUT.pin2
  N12: OT2.B, ROUT11.Pin_1
  R1: OT2.C, OUTPUT.pin3
  N13: OT3.B, ROUT21.Pin_1
  R2: OT3.C, OUTPUT.pin4
  N14: OT4.B, ROUT31.Pin_1
  R3: OT4.C, OUTPUT.pin5
  N15: ROUT01.Pin_0, O0.Pin_3
  N16: ROUT11.Pin_0, O1.Pin_3
  N17: ROUT21.Pin_0, O2.Pin_3
  N18: ROUT31.Pin_0, O3.Pin_3
  B0: RI01.Pin_0, INPUT.pin1
  N19: RI01.Pin_1, IN0.Pin_1
  B1: RI11.Pin_0, INPUT.pin2
  N20: RI11.Pin_1, IN1.Pin_1
  B2: RI21.Pin_0, INPUT.pin3
  N21: RI21.Pin_1, IN2.Pin_1
  B3: RI31.Pin_0, INPUT.pin4
  N22: RI31.Pin_1, IN3.Pin_1
  N23: STSR.Pin_1, LED1.cathode

notes:
  OUTPUT CKT
  MAIN BOOARD, 1.0
  OUTPUT, 1.0
  STS
  OUT0
  OUT1
  OUT2
  OUT3
  VDD
  GND
  IN0
  IN1
  IN2
  IN3
  RX
  TX
  VIN
  VCC
